# Fritzing sketch AccelerometerSensor (saved by Fritzing 0.8.3b)

parts:
  Part1 = Arduino Uno (Rev3)
  3-Axis_Accelerometer1 = 3-Axis Accelerometer Breakout - MMA8452Q

nets:
  N1: Part1.ICSP_MISO, Part1.D12/MISO, 3-Axis_Accelerometer1.SCL
  N2: Part1.ICSP_SCK, Part1.D13/SCK, 3-Axis_Accelerometer1.I2
  N3: Part1.ICSP_MOSI, Part1.D11_PWM/MOSI, 3-Axis_Accelerometer1.I1
  GND: Part1.GND, 3-Axis_Accelerometer1.GND
  N4: Part1.D10_PWM/SS, 3-Axis_Accelerometer1.SDA
  3V3: Part1.3V3, 3-Axis_Accelerometer1.3.3V
