# Fritzing sketch AccelerometerSensor_Dual (saved by Fritzing 0.8.3b)
breadboards: 1

parts:
  Part1 = Arduino Uno (Rev3)
  3-Axis_Accelerometer1 = 3-Axis Accelerometer Breakout - MMA8452Q
  3-Axis_Accelerometer2 = 3-Axis Accelerometer Breakout - MMA8452Q

nets:
  N1: Part1.ICSP_MISO, Part1.D12/MISO, 3-Axis_Accelerometer1.SCL, 3-Axis_Accelerometer2.SCL
  N2: Part1.ICSP_SCK, Part1.D13/SCK, 3-Axis_Accelerometer1.I2, 3-Axis_Accelerometer2.I2
  N3: Part1.ICSP_MOSI, Part1.D11_PWM/MOSI, 3-Axis_Accelerometer1.I1, 3-Axis_Accelerometer2.I1
  GND: Part1.GND, 3-Axis_Accelerometer1.GND, 3-Axis_Accelerometer2.GND
  N4: Part1.D2, 3-Axis_Accelerometer2.SDA
  N5: Part1.D3_PWM, 3-Axis_Accelerometer1.SDA
  3.3V: Part1.3V3, 3-Axis_Accelerometer1.3.3V, 3-Axis_Accelerometer2.3.3V
