# Fritzing sketch BodyMovementSensors (saved by Fritzing 0.8.3b)
breadboards: 1

parts:
  U2 = XBEE-1 [package=xbee-1_lock]
  R2 = Resistor [tolerance=±5% resistance=10k package=THT]
  R3 = Textile Stretch Sensor [part_number=PW052]
  R4 = Resistor [tolerance=±5% resistance=10k package=THT]
  J2 = Basic Force Sensing Resistor (FSR) [package=THT]
  Part7 = Arduino Uno (Rev3)
  U3 = LIS331 [package=lga16-3mm]
  U4 = LIS331 [package=lga16-3mm]
  R6 = Textile Stretch Sensor [part_number=PW052]
  R7 = Resistor [tolerance=±5% resistance=10k package=THT]
  U5 = mystery part, 3 pins [chip_label=PulseSensor]
  U6 = mystery part, 2 pins [chip_label="GSR sensor pads"]
  R5 = Resistor [tolerance=±5% resistance=10k package=THT]

nets:
  VDD: U2.VDD, J2.pin_1, Part7.3V3, U3.VDD, U4.VDDR, U5.pin1
  N1: U2.DOUT, Part7.D1/TX
  N2: U2.DIN, Part7.D0/RX
  GND: U2.GND, R2.Pin_1, R4.Pin_1, Part7.GND, U3.GND, U4.GND, R7.Pin_1, U5.pin2, R5.Pin_1
  N3: R2.Pin_0, Part7.A3, U6.pin2
  N4: R3.pin_1, R4.Pin_0, Part7.A0
  N5: J2.pin_0, Part7.A1, R5.Pin_0
  N6: Part7.A2, R6.pin_1, R7.Pin_0
  N7: Part7.A4/SDA, U5.pin3
  N8: Part7.ICSP_SCK, Part7.D13/SCK, U3.SCL_SPC, U4.SCL_SPC
  N9: Part7.D11_PWM/MOSI, U3.SA0_SDO, U4.SA0_SDO
  N10: Part7.D12/MISO, U3.SDA_SDI, U4.SDA_SDI
  N11: Part7.D2, U4.CS
  N12: Part7.D4, U3.CS
  N13: Part7.5V, U6.pin1

notes:
  3.3V
  5V
