# Fritzing sketch ConductiveRubberSensor (saved by Fritzing 0.8.3b)
breadboards: 1

parts:
  Part1 = Arduino Uno (Rev3)
  R1 = Resistor [tolerance=±5% resistance=10k package=THT]
  R2 = Textile Stretch Sensor [part_number=PW052]

nets:
  N1: Part1.A0, R1.Pin_0, R2.pin_1
  N2: Part1.GND, R1.Pin_1
  N3: Part1.3V3, R2.pin_0
