# Fritzing sketch GalvanicSkinResponseSensor (saved by Fritzing 0.8.3b)
breadboards: 1

parts:
  Part1 = Arduino Uno (Rev3)
  R1 = Resistor [tolerance=±5% resistance=10k package=THT]

nets:
  N1: Part1.A0, R1.Pin_0
  N2: Part1.GND, R1.Pin_1

notes:
  Conductive surface
  (Copper or aluminium)
