# Fritzing sketch XBee (saved by Fritzing 0.8.3b)
breadboards: 1

parts:
  U1 = XBEE-1 [package=xbee-1_lock]
  Part1 = Arduino Uno (Rev3)

nets:
  VDD: U1.VDD, Part1.3V3
  N1: U1.DOUT, Part1.D1/TX
  N2: U1.DIN, Part1.D0/RX
  GND: U1.GND, Part1.GND
